# Fritzing sketch cafe automatico taok (saved by Fritzing 0.8.7b)
breadboards: 1

parts:
  LCD1 = LCD screen
  U3 = POT [package=pot_alpha_rv16af-20]
  U4 = 2-Channel 5v Relay Shield [package=relay-2ch5v10a]
  VCC1 = 4 x AAA Battery Mount
  Part2 = Real Time Clock Module - DS1307 RTC Breakout Board
  Part1 = Arduino Uno (Rev3)

nets:
  GND: LCD1.VSS, LCD1.R/W, LCD1.LED-, U3.E, U4.GND, VCC1.-, Part2.GND, Part1.GND
  VDD: LCD1.VDD, LCD1.LED+, U3.A, Part1.5V
  N1: LCD1.V0, U3.S
  N2: LCD1.RS, Part1.D8
  N3: LCD1.E, Part1.D9_PWM
  N4: LCD1.DB4, Part1.D4
  N5: LCD1.DB5, Part1.D5_PWM
  N6: LCD1.DB6, Part1.D6_PWM
  N7: LCD1.DB7, Part1.D7
  VCC: U4.VCC, VCC1.+, Part2.5V
  N8: U4.IN1, Part1.D13/SCK
  N9: Part2.SCL, Part1.A5/SCL
  N10: Part2.SDA, Part1.A4/SDA

custom parts:
  2-Channel 5v Relay Shield: 2 Channel 5v Relay Shield w. 2x SPD-06VDC-SD-C
